// Digital circuit Computing_Sistem.dig as structural Verilog
module Computing_Sistem (
);

  wire or_1_out, undriven, undriven_2, undriven_3, undriven_4;

  or or_1 (or_1_out, undriven_4, undriven_3, undriven_2, undriven);
  Semafor semafor_1 ();  // open: Enable_counters, Reset_counters, Async_counter1, Async_counter2, Async_counter3, Flag_sensor1, Flag_sensor2, Flag_sensor3, Emergency_sensor, Set_verde, Set_galben, Set_rosu, Begin, Q_0_0, Q_0_1, Q_0_2, Q_0_3, Q_0_4, Q_0_5, Q_0_6, Q_0_7, Q_1_0, Q_1_1, Q_1_2, Q_1_3, Q_1_4, Q_1_5, Q_1_6, Q_1_7, Q_2_0, Q_2_1, Q_2_2, Q_2_3, Q_2_4, Q_2_5, Q_2_6, Q_2_7, Flag_1, Flag_2, Flag_3, Emergency, Color_green, Color_yellow, Color_red
  Semafor semafor_2 ();  // open: Enable_counters, Reset_counters, Async_counter2, Async_counter3, Async_counter1, Flag_sensor1, Flag_sensor2, Flag_sensor3, Emergency_sensor, Set_verde, Set_galben, Set_rosu, Begin, Q_0_0, Q_0_1, Q_0_2, Q_0_3, Q_0_4, Q_0_5, Q_0_6, Q_0_7, Q_1_0, Q_1_1, Q_1_2, Q_1_3, Q_1_4, Q_1_5, Q_1_6, Q_1_7, Q_2_0, Q_2_1, Q_2_2, Q_2_3, Q_2_4, Q_2_5, Q_2_6, Q_2_7, Flag_1, Flag_2, Flag_3, Emergency, Color_green, Color_yellow, Color_red
  Semafor semafor_3 ();  // open: Enable_counters, Reset_counters, Async_counter2, Async_counter3, Async_counter1, Flag_sensor1, Flag_sensor2, Flag_sensor3, Emergency_sensor, Set_verde, Set_galben, Set_rosu, Begin, Q_0_0, Q_0_1, Q_0_2, Q_0_3, Q_0_4, Q_0_5, Q_0_6, Q_0_7, Q_1_0, Q_1_1, Q_1_2, Q_1_3, Q_1_4, Q_1_5, Q_1_6, Q_1_7, Q_2_0, Q_2_1, Q_2_2, Q_2_3, Q_2_4, Q_2_5, Q_2_6, Q_2_7, Flag_1, Flag_2, Flag_3, Emergency, Color_green, Color_yellow, Color_red
  Semafor semafor_4 ();  // open: Enable_counters, Reset_counters, Async_counter2, Async_counter3, Async_counter1, Flag_sensor1, Flag_sensor2, Flag_sensor3, Emergency_sensor, Set_verde, Set_galben, Set_rosu, Begin, Q_0_0, Q_0_1, Q_0_2, Q_0_3, Q_0_4, Q_0_5, Q_0_6, Q_0_7, Q_1_0, Q_1_1, Q_1_2, Q_1_3, Q_1_4, Q_1_5, Q_1_6, Q_1_7, Q_2_0, Q_2_1, Q_2_2, Q_2_3, Q_2_4, Q_2_5, Q_2_6, Q_2_7, Flag_1, Flag_2, Flag_3, Emergency, Color_green, Color_yellow, Color_red

  // Notes on the sheet:
  //   exp
endmodule
